# Fritzing sketch L298N_Fritzing_File (saved by Fritzing 0.7.7b)
breadboards: 1

parts:
  Arduino1 = Arduino
  U1 = mystery part, 7 pins [chip_label=?]
  U2 = mystery part, 8 pins [chip_label=?]
  R2 = Resistor [tolerance=±5% resistance=220 package=THT]
  U3 = mystery part, 3 pins [chip_label=?]
  R1 = Resistor [tolerance=±5% resistance=220 package=THT]
  U5 = mystery part, 3 pins [chip_label=?]
  U6 = mystery part, 3 pins [chip_label=?]
  U7 = mystery part, 3 pins [chip_label=?]
  U8 = mystery part, 3 pins [chip_label=?]
  D1 = Rectifier Diode [part_number=1N4001 package="300 mil [THT]"]
  D2 = Rectifier Diode [part_number=1N4001 package="300 mil [THT]"]
  D3 = Rectifier Diode [part_number=1N4001 package="300 mil [THT]"]  # not connected
  D4 = Rectifier Diode [part_number=1N4001 package="300 mil [THT]"]
  U9 = mystery part, 3 pins [chip_label=?]
  U10 = mystery part, 2 pins [chip_label=?]
  U11 = mystery part, 2 pins [chip_label=?]
  D6 = Rectifier Diode [part_number=1N4001 package="300 mil [THT]"]
  U12 = mystery part, 1 pin [chip_label=?]
  U13 = mystery part, 1 pin [chip_label=?]
  U14 = mystery part, 1 pin [chip_label=?]  # not connected
  U15 = mystery part, 1 pin [chip_label=?]
  D7 = Rectifier Diode [part_number=1N4001 package="300 mil [THT]"]
  U16 = mystery part, 1 pin [chip_label=?]
  U17 = mystery part, 1 pin [chip_label=?]
  D8 = Rectifier Diode [part_number=1N4001 package="300 mil [THT]"]
  D9 = Rectifier Diode [part_number=1N4001 package="300 mil [THT]"]

nets:
  N1: Arduino1.GND, U1.pin4, R2.Pin_0, U3.pin2, R1.Pin_1, U5.pin2, U5.pin3
  N2: Arduino1.D11, U2.pin4
  N3: Arduino1.D10, U2.pin3
  N4: Arduino1.D6, U1.pin5
  N5: Arduino1.D5, U1.pin6
  N6: Arduino1.VIN, U3.pin1, U17.pin1
  N7: U1.pin1, U8.pin2, D2.cathode, D4.anode
  N8: U1.pin3, U2.pin5, U2.pin6, U16.pin1
  N9: U1.pin7, U12.pin1
  N10: U2.pin1, R1.Pin_0
  N11: U2.pin2, U8.pin3, D1.cathode
  N12: U2.pin7, U11.pin1, D6.cathode
  N13: U2.pin8, R2.Pin_1
  N14: U3.pin3, U5.pin1, U9.pin1
  N15: U6.pin2, U10.pin1
  N16: U6.pin3, U10.pin2
  N17: U7.pin1, U9.pin2
  N18: U7.pin2, U7.pin3, U9.pin3
  N19: D1.anode, D6.anode
  N20: D2.anode, D8.anode
  N21: U11.pin2, U13.pin1, D7.anode
  N22: U15.pin1, D7.cathode, D9.cathode
